# Fritzing sketch wiring (saved by Fritzing 0.9.3b)
circuit board: 6.7832cm x 5.54648cm

parts:
  Mod1 = Raspberry Pi Pico
  RTC = Tiny RTC - DS1307 Breakout Board
  Logger_Toggle = SWITCH_SPDT [package=kps-1290]
  µJST_PWR = Header 2 [package=jst-2-pth-ns]
  µJST_SM0 = Header 3 [package=jst-3-smd]
  µJST_SM1 = Header 3 [package=jst-3-smd]
  µJST_SM2 = Header 3 [package=jst-3-smd]
  µJST_UART = Header 2 [package=jst-2-pth-kit]
  µJST_DHT = Header 3 [package=jst-3-smd]
  A1 = Micro SD card reader
  LED = RGB LED (com. anode, rbg) [package="5 mm [THT]"]

nets:
  N1: Mod1.pin_1, µJST_UART.1
  N2: Mod1.pin_3, Mod1.pin_8, Mod1.pin_13, Mod1.pin_18, Mod1.pin_23, Mod1.pin_28, Mod1.pin_33, Mod1.pin_38, Mod1.pin_42, RTC.GND#21, µJST_PWR.1, µJST_SM0.2, µJST_SM1.2, µJST_SM2.2, µJST_UART.2, A1.Pin_6, LED.common_anode
  N3: Mod1.pin_4, A1.Pin_4
  N4: Mod1.pin_5, A1.Pin_3
  N5: Mod1.pin_6, A1.Pin_5
  N6: Mod1.pin_7, A1.Pin_2
  N7: Mod1.pin_9, RTC.SDA
  N8: Mod1.pin_10, RTC.SCL
  N9: Mod1.pin_12, µJST_DHT.1
  N10: Mod1.pin_16, LED.green_cathode
  N11: Mod1.pin_17, LED.blue_cathode
  N12: Mod1.pin_19, LED.red_cathode
  N13: Mod1.pin_20, Logger_Toggle.P
  N14: Mod1.pin_31, µJST_SM2.1
  N15: Mod1.pin_32, µJST_SM1.1
  N16: Mod1.pin_34, µJST_SM0.1
  N17: Mod1.pin_35, µJST_SM0.3, µJST_SM1.3, µJST_SM2.3
  N18: Mod1.pin_36, RTC.VCC#20, Logger_Toggle.S, A1.Pin_1
  N19: Mod1.pin_39, µJST_PWR.2
  N20: RTC.VCC#14, µJST_DHT.2
  N21: RTC.GND#15, µJST_DHT.3

custom parts:
  Raspberry Pi Pico: Raspberry Pi Pico. Based around the RP2040 microcontroller the Pico is a low cost microcontroller device bringing Raspberry Pi quality, cost, and easy of use to the microcontroller space. Jan 2021, Split part in to two versions: SMD (this one) and tht. This one is single sided and uses the castellation pads to solder the module to the board (no holes, other than for the USB connector!). The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
  Tiny RTC - DS1307 Breakout Board: The Tiny RTC is a breakout board for the Dallas Semiconductor/Maxim Integrated DS1307 real-time clock. The DS1307 counts seconds, minutes, hours, date of the month, month, day of the week, and year (with compensation for leap-years). The breakout board also has space for a DS18B20 digital thermometer.
  Micro SD card reader: Micro SD card reader.
