# Fritzing sketch pico_sketchboard (saved by Fritzing 0.9.3b)
breadboards: 1

parts:
  Pico_H = Raspberry Pi Pico H
  Capacitive_Soil_Moisture_Sensor1 = DFRobot Capacitive Soil Moisture Sensor V1.0 [part_number=SEN0193]
  Capacitive_Soil_Moisture_Sensor3 = DFRobot Capacitive Soil Moisture Sensor V1.0 [part_number=SEN0193]
  Capacitive_Soil_Moisture_Sensor2 = DFRobot Capacitive Soil Moisture Sensor V1.0 [part_number=SEN0193]
  DHT11 = DHT11 Humitidy and Temperature Sensor (3 pins)

nets:
  GND: Pico_H.GND, Capacitive_Soil_Moisture_Sensor1.GND, Capacitive_Soil_Moisture_Sensor3.GND, Capacitive_Soil_Moisture_Sensor2.GND, DHT11.Gnd
  N1: Pico_H.GP28_A2, Capacitive_Soil_Moisture_Sensor1.A
  N2: Pico_H.GP27_A1, Capacitive_Soil_Moisture_Sensor3.A
  N3: Pico_H.GP26_A0, Capacitive_Soil_Moisture_Sensor2.A
  N4: Pico_H.GP17, DHT11.Plus
  VCC: Pico_H.GP16, Capacitive_Soil_Moisture_Sensor1.VCC, Capacitive_Soil_Moisture_Sensor3.VCC, Capacitive_Soil_Moisture_Sensor2.VCC
  N5: Pico_H.GP15, DHT11.Signal

custom parts:
  Raspberry Pi Pico H: Raspberry Pi Pico H. Based around the RP2040 microcontroller the Pico H is a low cost microcontroller device bringing Raspberry Pi quality, cost, and easy of use to the microcontroller space.
  DFRobot Capacitive Soil Moisture Sensor V1.0: DFRobot Capacitive Soil Moisture Sensor V1.0 This product measures soil moisture levels by capacitive sensing, rather than resistive sensing like other types of moisture sensor. It is made of a corrosion resistant material giving it a long service life. Insert it into soil and impress your friends with the real-time soil moisture data! The product includes an on-board voltage regulator which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
  DHT11 Humitidy and Temperature Sensor (3 pins): DHT11 Humidity and Temperature Sensor (3 pins).
